# Fritzing sketch ticking bomb (saved by Fritzing 0.9.6b)
circuit board: 8.46667cm x 5.64444cm
breadboards: 1

parts:
  555 = Resistor [tolerance=±5% power=0.25 resistance=47k package=THT]
  C2 = Electrolytic Capacitor [capacitance=10µF voltage=35V package="100 mil [THT, electrolytic]"]
  C3 = Electrolytic Capacitor [capacitance=10µF voltage=35V package="100 mil [THT, electrolytic]"]
  U1 = 555 Timer [package="DIP8 [THT]"]
  SPKR1 = Loudspeaker
  VCC1 = 4 x AAA Battery Mount

nets:
  N1: 555.Pin_0, C3.+, U1.Output
  N2: 555.Pin_1, C2.+, U1.Trigger, U1.Threshold
  N3: C2.-, C3.-, U1.Ground, SPKR1.pin1, SPKR1.pin2
  N4: U1.Reset, VCC1.-
  N5: U1.Vcc_Supply_Voltage, VCC1.+
